// Digital circuit instruction_register_and_control_logic_with_flags.dig as structural Verilog
module instruction_register_and_control_logic_with_flags (
  input  I_0,
  input  C,
  input  I_1,
  input  I_2,
  input  I_3,
  input  Z_flag,
  input  S_flag,
  input  C_flag,
  output SGN,
  output ORI,
  output SUB,
  output ALU,
  output BRO,
  output BRI,
  output ARO,
  output ARI,
  output PCO,
  output PCI,
  output PCE,
  output HLT,
  output ADR,
  output RMI,
  output RMO,
  output IRI,
  output IRO,
  output FLG
);

  wire [1:0] counter_1_out;

  Counter #(.Bits(2)) counter_1 (.en(1'b1), .C(C), .clr(1'b0), .out(counter_1_out));  // open: ovf
  LookUpTable #(.Bits(18)) lookuptable_1 (
    .in0(counter_1_out[0]), .in1(counter_1_out[1]), .in2(I_0), .in3(I_1), .in4(I_2), .in5(I_3), .in6(Z_flag),
    .in7(S_flag), .in8(C_flag),
    .out({HLT, ADR, RMI, RMO, FLG, IRO, IRI, ORI, SGN, SUB, ALU, BRO, BRI, ARO, ARI, PCO, PCE, PCI}));

  // Notes on the sheet:
  //   Instruction Register, Control Logic with Flag Input
  //   contents of lookuptable_1 (hex, n*v repeats v):
  //   10004,4802,0,0,10004,4802,11000,4008,10004,4802,1008,0,10004,4802
  //   ,11000,4020,10004,4802,1020,0,10004,4802,11000,8010,10004,4802
  //   ,11000,8040,10004,4802,2000,88,10004,4802,2100,188,10004,4802
  //   ,1001,0,10004,4802,0,0,10004,4802,0,0,10004,4802,0,0,10004,4802
  //   ,11000,4400,10004,4802,11000,4600,10004,4802,20000,0,10004,4802
  //   ,0,0,10004,4802,11000,4008,10004,4802,1008,0,10004,4802,11000
  //   ,4020,10004,4802,1020,0,10004,4802,11000,8010,10004,4802,11000
  //   ,8040,10004,4802,2000,88,10004,4802,2100,188,10004,4802,1001,0
  //   ,10004,4802,1001,0,10004,4802,0,0,10004,4802,0,0,10004,4802,11000
  //   ,4400,10004,4802,11000,4600,10004,4802,20000,0,10004,4802,0,0
  //   ,10004,4802,11000,4008,10004,4802,1008,0,10004,4802,11000,4020
  //   ,10004,4802,1020,0,10004,4802,11000,8010,10004,4802,11000,8040
  //   ,10004,4802,2000,88,10004,4802,2100,188,10004,4802,1001,0,10004
  //   ,4802,0,0,10004,4802,1001,0,10004,4802,0,0,10004,4802,11000,4400
  //   ,10004,4802,11000,4600,10004,4802,20000,0,10004,4802,0,0,10004
  //   ,4802,11000,4008,10004,4802,1008,0,10004,4802,11000,4020,10004
  //   ,4802,1020,0,10004,4802,11000,8010,10004,4802,11000,8040,10004
  //   ,4802,2000,88,10004,4802,2100,188,10004,4802,1001,0,10004,4802
  //   ,1001,0,10004,4802,1001,0,10004,4802,0,0,10004,4802,11000,4400
  //   ,10004,4802,11000,4600,10004,4802,20000,0,10004,4802,0,0,10004
  //   ,4802,11000,4008,10004,4802,1008,0,10004,4802,11000,4020,10004
  //   ,4802,1020,0,10004,4802,11000,8010,10004,4802,11000,8040,10004
  //   ,4802,2000,88,10004,4802,2100,188,10004,4802,1001,0,10004,4802
  //   ,0,0,10004,4802,0,0,10004,4802,1001,0,10004,4802,11000,4400,10004
  //   ,4802,11000,4600,10004,4802,20000,0,10004,4802,0,0,10004,4802
  //   ,11000,4008,10004,4802,1008,0,10004,4802,11000,4020,10004,4802
  //   ,1020,0,10004,4802,11000,8010,10004,4802,11000,8040,10004,4802
  //   ,2000,88,10004,4802,2100,188,10004,4802,1001,0,10004,4802,1001
  //   ,0,10004,4802,0,0,10004,4802,1001,0,10004,4802,11000,4400,10004
  //   ,4802,11000,4600,10004,4802,20000,0,10004,4802,0,0,10004,4802
  //   ,11000,4008,10004,4802,1008,0,10004,4802,11000,4020,10004,4802
  //   ,1020,0,10004,4802,11000,8010,10004,4802,11000,8040,10004,4802
  //   ,2000,88,10004,4802,2100,188,10004,4802,1001,0,10004,4802,0,0
  //   ,10004,4802,1001,0,10004,4802,1001,0,10004,4802,11000,4400,10004
  //   ,4802,11000,4600,10004,4802,20000,0,10004,4802,0,0,10004,4802
  //   ,11000,4008,10004,4802,1008,0,10004,4802,11000,4020,10004,4802
  //   ,1020,0,10004,4802,11000,8010,10004,4802,11000,8040,10004,4802
  //   ,2000,88,10004,4802,2100,188,10004,4802,1001,0,10004,4802,1001
  //   ,0,10004,4802,1001,0,10004,4802,1001,0,10004,4802,11000,4400,10004
  //   ,4802,11000,4600,10004,4802,20000
endmodule

/* Test case Control Logic with Flag_Test:
		C_flag	S_flag	Z_flag	I_3	I_2	I_1	I_0	HLT	ADR	RMI	RMO	FLG	IRO	IRI	ORI	SGN	SUB	ALU	BRO	BRI	ARO	ARI	PCO	PCE	PCI	C
	# Set Counter																										
		0	0	0	0	0	0	0	X	X	X	X	X	X	X	X	X	X	X	X	X	X	X	X	X	X	C
		0	0	0	0	0	0	0	X	X	X	X	X	X	X	X	X	X	X	X	X	X	X	X	X	X	C
		0	0	0	0	0	0	0	X	X	X	X	X	X	X	X	X	X	X	X	X	X	X	X	X	X	C
# All but conditional jumps																											
loop(a,8)																											
	# NOOP																										
		bits(3,a)			0	0	0	0	0	1	0	0	0	0	0	0	0	0	0	0	0	0	0	1	0	0	C
		bits(3,a)			0	0	0	0	0	0	0	1	0	0	1	0	0	0	0	0	0	0	0	0	1	0	C
		bits(3,a)			0	0	0	0	0	0	0	0	0	0	0	0	0	0	0	0	0	0	0	0	0	0	C
		bits(3,a)			0	0	0	0	0	0	0	0	0	0	0	0	0	0	0	0	0	0	0	0	0	0	C
	# LDAR																										
		bits(3,a)			0	0	0	1	0	1	0	0	0	0	0	0	0	0	0	0	0	0	0	1	0	0	C
		bits(3,a)			0	0	0	1	0	0	0	1	0	0	1	0	0	0	0	0	0	0	0	0	1	0	C
		bits(3,a)			0	0	0	1	0	1	0	0	0	1	0	0	0	0	0	0	0	0	0	0	0	0	C
		bits(3,a)			0	0	0	1	0	0	0	1	0	0	0	0	0	0	0	0	0	0	1	0	0	0	C
	# LDAD																										
		bits(3,a)			0	0	1	0	0	1	0	0	0	0	0	0	0	0	0	0	0	0	0	1	0	0	C
		bits(3,a)			0	0	1	0	0	0	0	1	0	0	1	0	0	0	0	0	0	0	0	0	1	0	C
		bits(3,a)			0	0	1	0	0	0	0	0	0	1	0	0	0	0	0	0	0	0	1	0	0	0	C
		bits(3,a)			0	0	1	0	0	0	0	0	0	0	0	0	0	0	0	0	0	0	0	0	0	0	C
	# LDBR																										
		bits(3,a)			0	0	1	1	0	1	0	0	0	0	0	0	0	0	0	0	0	0	0	1	0	0	C
		bits(3,a)			0	0	1	1	0	0	0	1	0	0	1	0	0	0	0	0	0	0	0	0	1	0	C
		bits(3,a)			0	0	1	1	0	1	0	0	0	1	0	0	0	0	0	0	0	0	0	0	0	0	C
		bits(3,a)			0	0	1	1	0	0	0	1	0	0	0	0	0	0	0	0	1	0	0	0	0	0	C
	# LDBD																										
		bits(3,a)			0	1	0	0	0	1	0	0	0	0	0	0	0	0	0	0	0	0	0	1	0	0	C
		bits(3,a)			0	1	0	0	0	0	0	1	0	0	1	0	0	0	0	0	0	0	0	0	1	0	C
		bits(3,a)			0	1	0	0	0	0	0	0	0	1	0	0	0	0	0	0	1	0	0	0	0	0	C
		bits(3,a)			0	1	0	0	0	0	0	0	0	0	0	0	0	0	0	0	0	0	0	0	0	0	C
	# SAVA																										
		bits(3,a)			0	1	0	1	0	1	0	0	0	0	0	0	0	0	0	0	0	0	0	1	0	0	C
		bits(3,a)			0	1	0	1	0	0	0	1	0	0	1	0	0	0	0	0	0	0	0	0	1	0	C
		bits(3,a)			0	1	0	1	0	1	0	0	0	1	0	0	0	0	0	0	0	0	0	0	0	0	C
		bits(3,a)			0	1	0	1	0	0	1	0	0	0	0	0	0	0	0	0	0	1	0	0	0	0	C
	# SAVB																										
		bits(3,a)			0	1	1	0	0	1	0	0	0	0	0	0	0	0	0	0	0	0	0	1	0	0	C
		bits(3,a)			0	1	1	0	0	0	0	1	0	0	1	0	0	0	0	0	0	0	0	0	1	0	C
		bits(3,a)			0	1	1	0	0	1	0	0	0	1	0	0	0	0	0	0	0	0	0	0	0	0	C
		bits(3,a)			0	1	1	0	0	0	1	0	0	0	0	0	0	0	0	1	0	0	0	0	0	0	C
	# ADAB																										
		bits(3,a)			0	1	1	1	0	1	0	0	0	0	0	0	0	0	0	0	0	0	0	1	0	0	C
		bits(3,a)			0	1	1	1	0	0	0	1	0	0	1	0	0	0	0	0	0	0	0	0	1	0	C
		bits(3,a)			0	1	1	1	0	0	0	0	1	0	0	0	0	0	0	0	0	0	0	0	0	0	C
		bits(3,a)			0	1	1	1	0	0	0	0	0	0	0	0	0	0	1	0	0	0	1	0	0	0	C
	# SUAB																										
		bits(3,a)			1	0	0	0	0	1	0	0	0	0	0	0	0	0	0	0	0	0	0	1	0	0	C
		bits(3,a)			1	0	0	0	0	0	0	1	0	0	1	0	0	0	0	0	0	0	0	0	1	0	C
		bits(3,a)			1	0	0	0	0	0	0	0	1	0	0	0	0	1	0	0	0	0	0	0	0	0	C
		bits(3,a)			1	0	0	0	0	0	0	0	0	0	0	0	0	1	1	0	0	0	1	0	0	0	C
	# JMPA																										
		bits(3,a)			1	0	0	1	0	1	0	0	0	0	0	0	0	0	0	0	0	0	0	1	0	0	C
		bits(3,a)			1	0	0	1	0	0	0	1	0	0	1	0	0	0	0	0	0	0	0	0	1	0	C
		bits(3,a)			1	0	0	1	0	0	0	0	0	1	0	0	0	0	0	0	0	0	0	0	0	1	C
		bits(3,a)			1	0	0	1	0	0	0	0	0	0	0	0	0	0	0	0	0	0	0	0	0	0	C
	# OUTU																										
		bits(3,a)			1	1	0	1	0	1	0	0	0	0	0	0	0	0	0	0	0	0	0	1	0	0	C
		bits(3,a)			1	1	0	1	0	0	0	1	0	0	1	0	0	0	0	0	0	0	0	0	1	0	C
		bits(3,a)			1	1	0	1	0	1	0	0	0	1	0	0	0	0	0	0	0	0	0	0	0	0	C
		bits(3,a)			1	1	0	1	0	0	0	1	0	0	0	1	0	0	0	0	0	0	0	0	0	0	C
	# OUTS																										
		bits(3,a)			1	1	1	0	0	1	0	0	0	0	0	0	0	0	0	0	0	0	0	1	0	0	C
		bits(3,a)			1	1	1	0	0	0	0	1	0	0	1	0	0	0	0	0	0	0	0	0	1	0	C
		bits(3,a)			1	1	1	0	0	1	0	0	0	1	0	0	0	0	0	0	0	0	0	0	0	0	C
		bits(3,a)			1	1	1	0	0	0	0	1	0	0	0	1	1	0	0	0	0	0	0	0	0	0	C
	# HALT																										
		bits(3,a)			1	1	1	1	0	1	0	0	0	0	0	0	0	0	0	0	0	0	0	1	0	0	C
		bits(3,a)			1	1	1	1	0	0	0	1	0	0	1	0	0	0	0	0	0	0	0	0	1	0	C
		bits(3,a)			1	1	1	1	1	0	0	0	0	0	0	0	0	0	0	0	0	0	0	0	0	0	C
		bits(3,a)			1	1	1	1	0	0	0	0	0	0	0	0	0	0	0	0	0	0	0	0	0	0	C
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*/
