// Digital circuit control-logic.dig as structural Verilog
module control_logic (
  input  D_0,
  input  clk,
  input  D_1,
  input  D_2,
  input  D_3,
  input  D_4,
  input  D_5,
  input  D_6,
  input  D_7,
  input  instruction_i,
  input  instruction_o,
  output O_0,
  output O_1,
  output O_2,
  output O_3,
  output O_4,
  output O_5,
  output O_6,
  output O_7
);

  wire and_1_out, not_1_out;
  wire [2:0] add_1_s, Micro_q, multiplexer_1_out;
  wire [7:0] Instruction_q;

  Register #(.Bits(8)) Instruction (
    .D({D_7, D_6, D_5, D_4, D_3, D_2, D_1, D_0}), .C(clk), .en(instruction_i), .Q(Instruction_q));
  and and_1 (and_1_out, add_1_s[0], add_1_s[2]);
  Multiplexer #(.Bits(3)) multiplexer_1 (.sel(and_1_out), .in_0(add_1_s), .in_1(3'b000), .out(multiplexer_1_out));
  not not_1 (not_1_out, clk);
  Register #(.Bits(3)) Micro (.D(multiplexer_1_out), .C(not_1_out), .en(1'b1), .Q(Micro_q));
  assign {D_7, D_6, D_5, D_4, D_3, D_2, D_1, D_0} = instruction_o ? {4'b0000, Instruction_q[3:0]} : 8'bz;  // Driver driver_1
  Add #(.Bits(3)) add_1 (.a(Micro_q), .b(3'b001), .c_i(1'b0), .s(add_1_s));  // open: c_o
  LookUpTable #(.Bits(16)) lookuptable_1 (
    .in0(Micro_q[0]), .in1(Micro_q[1]), .in2(Micro_q[2]), .in3(Instruction_q[4]), .in4(Instruction_q[5]),
    .in5(Instruction_q[6]), .in6(Instruction_q[7]));  // open: out

  assign O_0 = D_0;
  assign O_1 = D_1;
  assign O_2 = D_2;
  assign O_3 = D_3;
  assign O_4 = D_4;
  assign O_5 = D_5;
  assign O_6 = D_6;
  assign O_7 = D_7;
endmodule
