// Digital circuit alu_flags_register.dig as structural Verilog
module alu_flags_register (
  input  A_0,
  input  A_1,
  input  A_2,
  input  A_3,
  input  A_4,
  input  A_5,
  input  A_6,
  input  A_7,
  input  sub,
  input  ALU_o,
  input  B_0,
  input  B_1,
  input  B_2,
  input  B_3,
  input  B_4,
  input  B_5,
  input  B_6,
  input  B_7,
  output O_0,
  output O_1,
  output O_2,
  output O_3,
  output O_4,
  output O_5,
  output O_6,
  output O_7
);

  wire [7:0] add_1_s, xor_1_out;

  assign xor_1_out = {B_7, B_6, B_5, B_4, B_3, B_2, B_1, B_0} ^ {8{sub}};  // XOr xor_1, 8 bits wide
  Add #(.Bits(8)) add_1 (
    .a({A_7, A_6, A_5, A_4, A_3, A_2, A_1, A_0}), .b(xor_1_out), .c_i(sub), .s(add_1_s));  // open: c_o
  assign {O_7, O_6, O_5, O_4, O_3, O_2, O_1, O_0} = ALU_o ? add_1_s : 8'bz;  // Driver driver_1

  // Notes on the sheet:
  //   Flags Register
endmodule

/* Test case flags register_test:
	A_i	A_o	B_i	B_o	ALU_o	sub	D_7	D_6	D_5	D_4	D_3	D_2	D_1	D_0	O_7	O_6	O_5	O_4	O_3	O_2	O_1	O_0	C
	0	0	0	0	0	0	0	0	0	0	0	0	0	0	0	0	0	0	0	0	0	0	C
	# Load 15 into A and Verify
	1	0	0	0	0	0	0	0	0	0	1	1	1	1	0	0	0	0	1	1	1	1	C
	0	1	0	0	0	0	Z	Z	Z	Z	Z	Z	Z	Z	0	0	0	0	1	1	1	1	C
	# Load 4 into B and Verify
	0	0	1	0	0	0	0	0	0	0	0	1	0	0	0	0	0	0	0	1	0	0	C
	0	0	0	1	0	0	Z	Z	Z	Z	Z	Z	Z	Z	0	0	0	0	0	1	0	0	C
	# Output Sum of A and B (15 + 4)
	0	0	0	0	1	0	Z	Z	Z	Z	Z	Z	Z	Z	0	0	0	1	0	0	1	1	C
	# Output Difference of A and B (15 - 4), Save in A, and Verify (note, after clock pulse, ALU otuput updates to the new A - B, thus it would be A - B - B)
	1	0	0	0	1	1	Z	Z	Z	Z	Z	Z	Z	Z	0	0	0	0	0	1	1	1	C
	0	1	0	0	0	0	Z	Z	Z	Z	Z	Z	Z	Z	0	0	0	0	1	0	1	1	C

# Add and Subtract Random Numbers
loop(a, 50)
	let r1 = random(255);
	let r2 = random(255);
	1	0	0	0	0	0	bits(8, r1)							bits(8, r1)							C
	0	0	1	0	0	0	bits(8, r2)							bits(8, r2)							C
	0	0	0	0	1	0	Z	Z	Z	Z	Z	Z	Z	Z	bits(8, r1+r2)							C
	0	0	0	0	1	1	Z	Z	Z	Z	Z	Z	Z	Z	bits(8, r1-r2)							C
end loop
*/
