// Digital circuit ram_register.dig as structural Verilog
module ram_register (
  input  C,
  input  D_3,
  input  D_2,
  input  D_1,
  input  D_0,
  input  RAM_i,
  input  RAM_o,
  input  REG_i,
  input  REG_o,
  input  A_1,
  input  A_0,
  output out_1,
  output out_7,
  output out_8,
  output out_9
);

  wire [3:0] register_1_q;

  RAMSinglePort #(.Bits(4)) ramsingleport_1 (.A({A_1, A_0}), .str(RAM_i), .C(C), .ld(RAM_o), .D({D_3, D_2, D_1, D_0}));
  Register #(.Bits(4)) register_1 (.D({D_3, D_2, D_1, D_0}), .C(C), .en(REG_i), .Q(register_1_q));
  assign {D_3, D_2, D_1, D_0} = REG_o ? register_1_q : 4'bz;  // Driver driver_1

  assign out_1 = D_0;
  assign out_7 = D_1;
  assign out_8 = D_3;
  assign out_9 = D_2;
endmodule
