// Digital circuit 2_and_4_multiplexer.dig as structural Verilog
module _2_and_4_multiplexer (
  input  input_a,
  input  input_b,
  input  select,
  input  input_w,
  input  input_x,
  input  input_y,
  input  input_z,
  input  select_b,
  input  select_a,
  output output_2,
  output output_4
);

  wire and_1_out, and_2_out, and_3_out, and_4_out, and_5_out, and_6_out;

  and and_1 (and_1_out, ~select, input_a);  // And
  and and_2 (and_2_out, select, input_b);
  and and_3 (and_3_out, ~select_b, ~select_a, input_w);  // And
  and and_4 (and_4_out, select_b, ~select_a, input_x);  // And
  and and_5 (and_5_out, ~select_b, select_a, input_y);  // And
  and and_6 (and_6_out, select_b, select_a, input_z);
  or or_1 (output_2, and_1_out, and_2_out);
  or or_2 (output_4, and_3_out, and_4_out, and_5_out, and_6_out);

  // Notes on the sheet:
  //   Two Bit Multiplexer
  //   Four Bit Multiplexer
endmodule

/* Test case 2 bit mux_test:
input_a	input_b	select	output_2
0	0	0	0
0	0	1	0
0	1	0	0
0	1	1	1
1	0	0	1
1	0	1	0
1	1	0	1
1	1	1	1
*/

/* Test case 4 bit mux_test:
input_w	input_x	input_y	input_z	select_a	select_b	output_4
0	0	0	0	0		0		0
0	0	0	0	0		1		0
0	0	0	0	1		0		0
0	0	0	0	1		1		0
0	0	0	1	0		0		0
0	0	0	1	0		1		0
0	0	0	1	1		0		0
0	0	0	1	1		1		1
0	0	1	0	0		0		0
0	0	1	0	0		1		0
0	0	1	0	1		0		1
0	0	1	0	1		1		0
0	0	1	1	0		0		0
0	0	1	1	0		1		0
0	0	1	1	1		0		1
0	0	1	1	1		1		1
0	1	0	0	0		0		0
0	1	0	0	0		1		1
0	1	0	0	1		0		0
0	1	0	0	1		1		0
0	1	0	1	0		0		0
0	1	0	1	0		1		1
0	1	0	1	1		0		0
0	1	0	1	1		1		1
0	1	1	0	0		0		0
0	1	1	0	0		1		1
0	1	1	0	1		0		1
0	1	1	0	1		1		0
0	1	1	1	0		0		0
0	1	1	1	0		1		1
0	1	1	1	1		0		1
0	1	1	1	1		1		1
1	0	0	0	0		0		1
1	0	0	0	0		1		0
1	0	0	0	1		0		0
1	0	0	0	1		1		0
1	0	0	1	0		0		1
1	0	0	1	0		1		0
1	0	0	1	1		0		0
1	0	0	1	1		1		1
1	0	1	0	0		0		1
1	0	1	0	0		1		0
1	0	1	0	1		0		1
1	0	1	0	1		1		0
1	0	1	1	0		0		1
1	0	1	1	0		1		0
1	0	1	1	1		0		1
1	0	1	1	1		1		1
1	1	0	0	0		0		1
1	1	0	0	0		1		1
1	1	0	0	1		0		0
1	1	0	0	1		1		0
1	1	0	1	0		0		1
1	1	0	1	0		1		1
1	1	0	1	1		0		0
1	1	0	1	1		1		1
1	1	1	0	0		0		1
1	1	1	0	0		1		1
1	1	1	0	1		0		1
1	1	1	0	1		1		0
1	1	1	1	0		0		1
1	1	1	1	0		1		1
1	1	1	1	1		0		1
1	1	1	1	1		1		1
*/
