// Digital circuit output_seven_segment.dig as structural Verilog
module output_seven_segment (
  input  D_0,
  input  D_1,
  input  D_2,
  input  D_3,
  input  D_4,
  input  D_5,
  input  D_6,
  input  D_7
);

  wire pulldown_1_out;
  wire [7:0] lookuptable_1_out;

  LookUpTable #(.Bits(8)) lookuptable_1 (
    .in0(D_0), .in1(D_1), .in2(D_2), .in3(D_3), .in4(D_4), .in5(D_5), .in6(D_6), .in7(D_7),
    .out(lookuptable_1_out));
  Seven_Seg #(.commonCathode("true")) seven_seg_1 (
    .a(lookuptable_1_out[0]), .b(lookuptable_1_out[1]), .c(lookuptable_1_out[2]), .d(lookuptable_1_out[3]),
    .e(lookuptable_1_out[4]), .f(lookuptable_1_out[5]), .g(lookuptable_1_out[6]), .dp(lookuptable_1_out[7]),
    .common(pulldown_1_out));
  PullDown pulldown_1 (.out(pulldown_1_out));

  // Notes on the sheet:
  //   contents of lookuptable_1 (hex, n*v repeats v):
  //   3f,6,5b,4f,66,6d
endmodule
