// Digital circuit program-counter.dig as structural Verilog
module program_counter (
  input  PC_o,
  input  PC_i,
  input  D_0,
  input  D_1,
  input  D_2,
  input  D_3,
  input  clk,
  input  PC_e,
  output O_0,
  output O_1,
  output O_2,
  output O_3
);

  wire or_1_out;
  wire [3:0] add_1_s, multiplexer_1_out, register_1_q;

  Multiplexer #(.Bits(4)) multiplexer_1 (
    .sel(PC_i), .in_0(add_1_s), .in_1({D_3, D_2, D_1, D_0}), .out(multiplexer_1_out));
  or or_1 (or_1_out, PC_e, PC_i);
  Register #(.Bits(4)) register_1 (.D(multiplexer_1_out), .C(clk), .en(or_1_out), .Q(register_1_q));
  Add #(.Bits(4)) add_1 (.a(register_1_q), .b(4'b0001), .c_i(1'b0), .s(add_1_s));  // open: c_o
  assign {D_3, D_2, D_1, D_0} = PC_o ? register_1_q : 4'bz;  // Driver driver_1

  assign O_0 = D_0;
  assign O_1 = D_1;
  assign O_2 = D_2;
  assign O_3 = D_3;

  // Notes on the sheet:
  //   Program Counter
endmodule
